// Logisim project cpu.circ as structural Verilog: 1 circuit, main circuit main
module main (
  input  [31:0] INSTRUCTION,
  input  CLOCK,
  output [31:0] PROGRAM_COUNTER,
  output [31:0] ra,
  output [31:0] sp,
  output [31:0] t0,
  output [31:0] t1,
  output [31:0] t2,
  output [31:0] s0,
  output [31:0] s1,
  output [31:0] a0
);

  wire [2:0] func3, imm_sel;
  wire [6:0] func7;
  wire [24:0] inst_reg;
  wire [31:0] adder_1_out, imm, RegFile_read_data_1, result;

  control_logic control_logic_1 (
    .ImmSel(imm_sel), .inst({func7, inst_reg[24:15], func3, inst_reg[11:0]}));  // open: BSel, BrUn, RegWEn, ASel, PCSel, BrLt, BrEq, ALUSel, MemRW, WBSel
  Adder #(.width(32)) adder_1 (.a(PROGRAM_COUNTER), .b(32'h4), .out(adder_1_out));  // open: cin, cout
  Register #(.width(32)) u_inst_reg (
    .D(INSTRUCTION), .clk(CLOCK), .Q({func7, inst_reg[24:15], func3, inst_reg[11:0]}));  // open: en, clr
  Register #(.width(32)) PC (.D(adder_1_out), .clk(CLOCK), .Q(PROGRAM_COUNTER));  // open: en, clr
  imm_gen imm_gen_1 (.ImmSel(imm_sel), .imm(imm), .inst({func7, inst_reg[24:15], func3, inst_reg[11:0]}));
  // Probe on imm
  // branch_comp branch_comp_1: pin names not known
  regfile_main RegFile (
    .rs2(inst_reg[24:20]), .rd(inst_reg[11:7]), .Read_Data_1(RegFile_read_data_1), .ra(ra), .sp(sp), .t0(t0),
    .t1(t1), .t2(t2), .s0(s0), .s1(s1), .a0(a0), .rs1(inst_reg[19:15]), .Write_Data(result), .RegWEn(1'b1),
    .clk(CLOCK));  // open: Read_Data_2
  alu Arithmetic_Logic_Unit (.ALUSel(4'b0000), .Result(result), .A(RegFile_read_data_1), .B(imm));
  // mem_main DMEM: pin names not known; wires that end beside it: CLOCK

  // Other names for the same wires on the sheet: clk = CLOCK; op[6:0] = inst_reg[6:0]; rd[4:0] = inst_reg[11:7];
  //   inst_reg (some bits) = {func7, func3}; r1[4:0] = inst_reg[19:15]; r2[4:0] = inst_reg[24:20]

  // Notes on the sheet:
  //   Output
  //   IMEM (do **NOT** move this)
  //   Inputs
  //   It is OK to move the PC, RegFile, ALU, MEM, Branch Comp, Imm Gen, and Control Logic to wherever is most convenient for you when constructing your CPU, and to delete this text
  //   Inputs/Outputs for testing. Do **NOT** move these.
endmodule
