// Logisim project imm_gen.circ as structural Verilog: 1 circuit, main circuit imm_gen
module imm_gen (
  input  [31:0] inst,
  input  [2:0] ImmSel,
  output [31:0] imm
);

  wire [31:0] bit_extender_3_out, bit_extender_4_out, bit_extender_5_out, BType, IType, JType, SType, UType;

  assign IType = {{20{inst[31]}}, inst[31:20]};  // Bit_Extender bit_extender_1
  assign SType = {{20{inst[31]}}, {inst[31:25], inst[11:7]}};  // Bit_Extender bit_extender_2
  assign bit_extender_3_out = {{20{inst[31]}}, {inst[31], inst[7], inst[30:25], inst[11:8]}};  // Bit_Extender bit_extender_3
  assign bit_extender_4_out = {{12{inst[31]}}, inst[31:12]};  // Bit_Extender bit_extender_4
  assign bit_extender_5_out = {{12{inst[31]}}, {inst[31], inst[19:12], inst[20], inst[30:21]}};  // Bit_Extender bit_extender_5
  Shifter #(.width(32)) shifter_1 (.in(bit_extender_3_out), .\dist (5'b00001), .out(BType));
  Shifter #(.width(32)) shifter_2 (.in(bit_extender_4_out), .\dist (5'b01100), .out(UType));
  Shifter #(.width(32)) shifter_3 (.in(bit_extender_5_out), .\dist (5'b00001), .out(JType));
  Multiplexer #(.select(3), .width(32), .enable("false")) multiplexer_1 (
    .in0(IType), .in1(IType), .in2(SType), .in4(UType), .in5(JType), .in6(BType), .in7(IType), .out(imm),
    .sel(ImmSel));  // open: in3

  // Notes on the sheet:
  //   INPUTS to your circuit
  //   DON'T CHANGE THE LOCATIONS OF THE INPUTS AND OUTPUTS!
  //   OUTPUT from your circuit
endmodule
